# Fritzing sketch microphon_amp_sdcard (saved by Fritzing 0.9.10b)
breadboards: 2

parts:
  MH-ET_LIVE_ESP32_DEVKIT1 = MH-ET LIVE ESP32 DEVKIT 38 pins
  Part1 = INMP441
  Part2 = Adafruit MAX98357A I2S 3W Class D Amplifier [part_number="Adafruit #3006"]
  microSD_Transflash1 = SparkFun - microSD Transflash

nets:
  N1: MH-ET_LIVE_ESP32_DEVKIT1.IO32, Part1.SCK
  N2: MH-ET_LIVE_ESP32_DEVKIT1.IO33, Part1.SD
  N3: MH-ET_LIVE_ESP32_DEVKIT1.IO25, Part1.WS
  N4: MH-ET_LIVE_ESP32_DEVKIT1.IO26, Part2.BCLK
  N5: MH-ET_LIVE_ESP32_DEVKIT1.IO27, Part2.LRCLK
  N6: MH-ET_LIVE_ESP32_DEVKIT1.IO23, microSD_Transflash1.DI
  N7: MH-ET_LIVE_ESP32_DEVKIT1.IO19, microSD_Transflash1.DO
  N8: MH-ET_LIVE_ESP32_DEVKIT1.IO18, microSD_Transflash1.SCK
  N9: MH-ET_LIVE_ESP32_DEVKIT1.IO5, microSD_Transflash1.CS
  N10: MH-ET_LIVE_ESP32_DEVKIT1.IO17, Part2.DIN
  N11: Part1.L/R, Part1.GND

custom parts:
  MH-ET LIVE ESP32 DEVKIT 38 pins: http://mh.nodebb.com/topic/2/mh-et-live-esp32-devkit
  INMP441: This is a simple breakout board for the INMP441 I2S MEMS microphone.
  Adafruit MAX98357A I2S 3W Class D Amplifier: Listen to this good news - we now have an all in one digital audio amp breakout board that works incredibly well with the Raspberry Pi! If you're looking for an easy and low cost way to get you digital sound files bumpin' then the MAX08357 I2S Amp Breakout is for you. It takes standard I2S digital audio input and, not only decodes it into analog, but also amplifies it directly into a speaker.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
