# Fritzing sketch oled_and_joystick (saved by Fritzing 0.9.10b)
breadboards: 2

parts:
  MH-ET_LIVE_ESP32_DEVKIT1 = MH-ET LIVE ESP32 DEVKIT 38 pins
  OLED1 = OLED 128x64 I2C Monochrome Display GND-VDD
  Part1 = Thumb Joystick

nets:
  N1: MH-ET_LIVE_ESP32_DEVKIT1.IO22, OLED1.SCK
  N2: MH-ET_LIVE_ESP32_DEVKIT1.IO21, OLED1.SDA
  N3: MH-ET_LIVE_ESP32_DEVKIT1.IO15, Part1.SEL
  GND: OLED1.GND, Part1.GND
  VDD: OLED1.VDD, Part1.VCC

custom parts:
  MH-ET LIVE ESP32 DEVKIT 38 pins: http://mh.nodebb.com/topic/2/mh-et-live-esp32-devkit
  OLED 128x64 I2C Monochrome Display GND-VDD: OLED 128x64 I2C Monochrome Display. Note: there are two variants of this part, this one is the GND VDD SCK SDA variant. The other is VDD GND SCK SDA. Make sure you select the part that matches your module as using the incorrect part will probably destroy your module! In addition the mounting holes are marked on silkscreen but not by default drilled. If you want drilled mounting holes, copy a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
